// Logisim project CAR_SECUTIRY_SYS.circ as structural Verilog: 1 circuit, main circuit main
module main (
  input  KEY,
  input  DOOR,
  input  SEATBELT
);

  wire and_1_out, and_2_out, and_3_out, not_1_out, not_2_out, or_1_out;

  not not_1 (not_1_out, DOOR);
  not not_2 (not_2_out, SEATBELT);
  and and_1 (and_1_out, KEY, DOOR, SEATBELT);
  and and_2 (and_2_out, KEY, not_1_out);
  and and_3 (and_3_out, KEY, not_2_out);
  LED led_1 (.in(and_1_out));
  or or_1 (or_1_out, and_2_out, and_3_out);
  LED led_2 (.in(or_1_out));

  // Notes on the sheet:
  //   ENGINE
  //   BUZZER
endmodule
